# Fritzing sketch breadboard (saved by Fritzing 0.9.6b)
circuit board: 8.46667cm x 5.64444cm
breadboards: 1

parts:
  BNO055 = 9-DOF Absolute Orientation IMU Fusion Breakout - BNO055
  J1 = T Cobbler Plus
  R1 = Resistor [tolerance=±5% resistance=220 package="0603 [SMD]"]  # not connected

nets:
  N1: BNO055.5.0V, BNO055.PS1_3V, J1.5.0V
  GND: BNO055.GND, J1.GND
  N2: BNO055.SDA_5V, J1.RXD
  N3: BNO055.SCL_5V, J1.TXD
  N4: BNO055.RST_5V, J1.#18

custom parts:
  9-DOF Absolute Orientation IMU Fusion Breakout - BNO055: A MEMS accelerometer, magnetometer and gyroscope on a single die with a high speed ARM Cortex-M0 based processor to digest all the sensor data, abstract the sensor fusion and real time requirements away, and spit out data you can use in quaternions, Euler angles or vectors.
  T Cobbler Plus: The T-Cobbler Plus is an add on prototyping board from Adafruit specifically designed for the Raspberry Pi B+ that can break out all those tasty power, GPIO, I2C and SPI pins from the 40-pin header onto a solderless breadboard. This set will make "cobbling together" prototypes with the Pi super easy. The T-Cobbler Plus can plug into any solderless breadboard.
